# Fritzing sketch rasp_l298_conn (saved by Fritzing 0.9.3b)

parts:
  U1 = L298 [package=multiwatt15]
  Right_Motor = DC Motor
  Left_Motor = DC Motor
  Battery_9v = Battery block 9V
  Raspberry_Pi_1 = Raspberry Pi 3 [part_number=RPI-3-V1.2]

nets:
  N1: U1.OUT1, Right_Motor.pin_2
  N2: U1.OUT2, Right_Motor.pin_1
  N3: U1.VS, Battery_9v.+
  N4: U1.IN1, Raspberry_Pi_1.GPIO27
  N5: U1.ENA, Raspberry_Pi_1.GPIO17
  N6: U1.IN2, Raspberry_Pi_1.GPIO22
  GND: U1.GND, Battery_9v.-, Raspberry_Pi_1.GND
  N7: U1.IN3, Raspberry_Pi_1.GPIO24
  N8: U1.ENB, Raspberry_Pi_1.GPIO23
  N9: U1.IN4, Raspberry_Pi_1.GPIO25
  N10: U1.OUT3, Left_Motor.pin_1
  N11: U1.OUT4, Left_Motor.pin_2

notes:
  if you will use battery which voltage be less than 5v, then you need to connect battery positive wire to L298's VLS pin
